# Fritzing sketch master (saved by Fritzing 0.9.3b)
breadboards: 1

parts:
  S1 = H-Bridge with L298N
  Part1 = Arduino Mega ADK (Rev3)
  VCC1 = 4 x AAA Battery Mount
  M1 = DC Motor
  M2 = DC Motor
  U3 = ESP8266 WiFi Module [part_number=ESP8266]
  Part2 = Bluetooth HC-05 Macho

nets:
  12V: S1.12V, Part1.VIN, VCC1.+
  N1: S1.GND, VCC1.-
  N2: S1.IN1, Part1.D6_PWM
  N3: S1.IN2, Part1.D5_PWM
  N4: S1.IN3, Part1.D11_PWM
  N5: S1.IN4, Part1.D3_PWM
  N6: S1.M1-01, M2.pin_2
  N7: S1.M1-02, M2.pin_1
  N8: S1.M2-01, M1.pin_2
  N9: S1.M2-02, M1.pin_1
  N10: Part1.D19/RX1, U3.TX
  N11: Part1.D18/TX1, U3.RX
  GND: Part1.GND, U3.GND, Part2.GND
  3V3: Part1.3V3, U3.XPD, U3.3.3V
  5V: Part1.5V, Part2.VCC
  N12: Part1.D0/RX0, Part2.TXD
  N13: Part1.D1/TX0, Part2.RXD

custom parts:
  H-Bridge with L298N: h-bridge
