# Fritzing sketch slave (saved by Fritzing 0.9.3b)
breadboards: 1

parts:
  Part3 = Arduino Mega ADK (Rev3)
  S2 = H-Bridge with L298N
  VCC2 = 4 x AAA Battery Mount
  M3 = DC Motor
  M4 = DC Motor
  Part4 = Bluetooth HC-05 Macho

nets:
  GND: Part3.GND, Part4.GND
  N1: Part3.D11_PWM, S2.IN3
  5V: Part3.5V, Part4.VCC
  VIN: Part3.VIN, S2.12V, VCC2.+
  N2: Part3.D0/RX0, Part4.TXD
  N3: Part3.D1/TX0, Part4.RXD
  N4: Part3.D3_PWM, S2.IN4
  N5: Part3.D5_PWM, S2.IN2
  N6: Part3.D6_PWM, S2.IN1
  N7: S2.GND, VCC2.-
  N8: S2.M1-01, M4.pin_2
  N9: S2.M1-02, M4.pin_1
  N10: S2.M2-01, M3.pin_2
  N11: S2.M2-02, M3.pin_1

custom parts:
  H-Bridge with L298N: h-bridge
